# Fritzing sketch Schema smart systems matrix schema versie (saved by Fritzing 0.9.2b)
breadboards: 1

parts:
  Onderdeel1 = Arduino Uno (Rev3)
  Onderdeel2 = Bluetooth HC-05 Macho
  IC1 = L293D [package=THT]
  VCC1 = Battery block 9V
  VCC2 = Battery block 9V
  Onderdeel4 = SRF05 Ultrasonic Rangefinder
  Onderdeel5 = SRF05 Ultrasonic Rangefinder
  Onderdeel6 = SRF05 Ultrasonic Rangefinder
  M1 = DC Motor
  M2 = DC Motor

nets:
  N1: Onderdeel1.D8, Onderdeel4.Echo
  N2: Onderdeel1.D9_PWM, Onderdeel4.Trig
  N3: Onderdeel1.D10_PWM/SS, Onderdeel5.Echo
  N4: Onderdeel1.D11_PWM/MOSI, Onderdeel5.Trig
  N5: Onderdeel1.D12/MISO, Onderdeel6.Echo
  N6: Onderdeel1.D13/SCK, Onderdeel6.Trig
  N7: Onderdeel1.D0/RX, Onderdeel2.TXD
  N8: Onderdeel1.D1/TX, Onderdeel2.RXD
  N9: Onderdeel1.D2, IC1.Enable_1
  N10: Onderdeel1.D3_PWM, IC1.In_1
  N11: Onderdeel1.D4, IC1.In_2
  N12: Onderdeel1.D5_PWM, IC1.Enable_2
  N13: Onderdeel1.D6_PWM, IC1.In_3
  N14: Onderdeel1.D7, IC1.In_4
  VCC: Onderdeel1.5V, Onderdeel2.VCC, Onderdeel4.VCC, Onderdeel5.VCC, Onderdeel6.VCC
  GND: Onderdeel1.GND, Onderdeel2.GND, VCC2.-, Onderdeel4.GND, Onderdeel5.GND, Onderdeel6.GND
  N15: Onderdeel1.VIN, VCC2.+
  N16: IC1.Out_1_(_Controlled_by_Enable_1_), M2.pin_2
  N17: IC1.0V, VCC1.-
  N18: IC1.Out_2_(_Controlled_by_Enable_1_), M2.pin_1
  N19: IC1.+Vmotor, IC1.+V, VCC1.+
  N20: IC1.Out_3_(_Controlled_by_Enable_2_), M1.pin_2
  N21: IC1.Out_4_(_Controlled_by_Enable_2_), M1.pin_1
