# Fritzing sketch smart systems autotje (saved by Fritzing 0.9.2b)
breadboards: 1

parts:
  Onderdeel1 = Arduino Uno (Rev3)
  M2 = DC Motor
  M3 = DC Motor
  Onderdeel3 = SRF05 Ultrasonic Rangefinder
  IC2 = L293D [package=THT]
  VCC1 = Battery block 9V
  Onderdeel2 = Bluetooth HC-05 Macho
  Onderdeel4 = SRF05 Ultrasonic Rangefinder
  Onderdeel5 = SRF05 Ultrasonic Rangefinder
  VCC2 = Battery block 9V

nets:
  N1: Onderdeel1.D8, IC2.In_3
  N2: Onderdeel1.D9_PWM, IC2.In_4
  N3: Onderdeel1.D10_PWM/SS, Onderdeel4.Echo
  N4: Onderdeel1.D11_PWM/MOSI, IC2.Enable_2
  N5: Onderdeel1.D12/MISO, Onderdeel3.Echo
  N6: Onderdeel1.D13/SCK, Onderdeel3.Trig
  N7: Onderdeel1.D0/RX, Onderdeel2.TXD
  N8: Onderdeel1.D1/TX, Onderdeel2.RXD
  N9: Onderdeel1.D2, Onderdeel5.Trig
  N10: Onderdeel1.D3_PWM, IC2.In_1
  N11: Onderdeel1.D4, IC2.In_2
  N12: Onderdeel1.D5_PWM, Onderdeel5.Echo
  N13: Onderdeel1.D6_PWM, IC2.Enable_1
  N14: Onderdeel1.D7, Onderdeel4.Trig
  VCC: Onderdeel1.5V, Onderdeel3.VCC, Onderdeel2.VCC, Onderdeel4.VCC, Onderdeel5.VCC
  GND: Onderdeel1.GND, Onderdeel3.GND, Onderdeel2.GND, Onderdeel4.GND, Onderdeel5.GND, VCC2.-
  N15: Onderdeel1.VIN, VCC2.+
  N16: M2.pin_1, IC2.Out_2_(_Controlled_by_Enable_1_)
  N17: M2.pin_2, IC2.Out_1_(_Controlled_by_Enable_1_)
  N18: M3.pin_1, IC2.Out_4_(_Controlled_by_Enable_2_)
  N19: M3.pin_2, IC2.Out_3_(_Controlled_by_Enable_2_)
  N20: IC2.0V, VCC1.-
  N21: IC2.+Vmotor, IC2.+V, VCC1.+
